# Fritzing sketch Wetterstation2.1 (saved by Fritzing 0.9.6b)
circuit board: 8.46667cm x 5.64444cm

parts:
  U1 = ESP8266 NodeMCU LoLin module
  Bauteil1 = BME280 Breakout

nets:
  N1: U1.D1, Bauteil1.SDI/SDA
  N2: U1.D2, Bauteil1.SCK/SCL
  3V3: U1.3V3, Bauteil1.3.3V
  GND: U1.GND, Bauteil1.GND

notes:
  NodeMCU
  TXD
  RXD
  GND
  2,5um
  5V
  1um
  NC

custom parts:
  ESP8266 NodeMCU LoLin module: ESP8266 based NodeMCU
