# Fritzing sketch Wetterstation3.1 (saved by Fritzing 0.9.6b)

parts:
  U2 = ESP8266 NodeMCU LoLin module
  Bauteil2 = BME280 Breakout
  WiFi-Control = LED - 5mm [color="Red (633nm)" package="5 mm [THT]"]
  Upload-Control = LED - 5mm [color="Red (633nm)" current=0.030 package="5 mm [THT]"]
  BME280-Control = LED - 5mm [color="Red (633nm)" current=0.030 package="5 mm [THT]"]
  Feinstaub-Control = LED - 5mm [color="Red (633nm)" current=0.030 package="5 mm [THT]"]

nets:
  N1: U2.D1, Bauteil2.SDI/SDA
  N2: U2.D2, Bauteil2.SCK/SCL
  3V3: U2.3V3, Bauteil2.3.3V
  GND: U2.GND, Bauteil2.GND, WiFi-Control.cathode, Upload-Control.cathode, BME280-Control.cathode, Feinstaub-Control.cathode
  N3: U2.D5, WiFi-Control.anode
  N4: U2.D6, Upload-Control.anode
  N5: U2.D7, BME280-Control.anode
  N6: U2.D8, Feinstaub-Control.anode

notes:
  NodeMCU
  TXD
  RXD
  GND
  2,5um
  5V
  1um
  NC

custom parts:
  ESP8266 NodeMCU LoLin module: ESP8266 based NodeMCU
